# Fritzing sketch Control (saved by Fritzing 0.9.3b)
breadboards: 1

parts:
  IC1 = L293D [package=THT]
  U1 = 74HC04_HEX_INVERTER [package=dil14]
  Power_On = LTE-302 [package=lte-302]
  Data_Receive = LTE-302 [package=lte-302]
  R1 = Resistor [tolerance=±5% resistance=220 package="0603 [SMD]"]
  R2 = Resistor [tolerance=±5% resistance=220 package="0603 [SMD]"]
  BAT1 = Battery Holders [package=battery-aa]
  IC2 = Voltage Regulator [package=to-220-alt]
  U2 = Vibration Motor- ROB-08449 [package=vibe-motor-10mm]
  U3 = Vibration Motor- ROB-08449 [package=vibe-motor-10mm]
  S2 = Pushbutton [package=THT]

nets:
  N1: IC1.Enable_1, IC1.Enable_2
  N2: IC1.In_1, U1.1A
  N3: IC1.Out_1_(_Controlled_by_Enable_1_), U2.+
  GND: IC1.0V
  N4: IC1.Out_2_(_Controlled_by_Enable_1_), U2.-
  N5: IC1.In_2, U1.1Y
  N6: IC1.+Vmotor, IC2.IN, S2.leg1
  N7: IC1.In_3, U1.2Y
  N8: IC1.Out_3_(_Controlled_by_Enable_2_), U3.-
  N9: IC1.Out_4_(_Controlled_by_Enable_2_), U3.+
  N10: IC1.In_4, U1.2A
  N11: IC1.+V, U1.VCC, IC2.OUT
  N12: U1.3A, R2.Pin_0
  N13: U1.3Y, R1.Pin_0
  N14: Power_On.A, R2.Pin_1
  N15: Power_On.C, Data_Receive.C
  N16: Data_Receive.A, R1.Pin_1
  N17: BAT1.-, S2.leg0
